# Fritzing sketch finalproject (saved by Fritzing 0.9.3b)
breadboards: 1

parts:
  V1 = DC Power [voltage=5]
  S1 = Pushbutton [package=THT]
  S2 = Pushbutton [package=THT]
  S3 = Pushbutton [package=THT]
  S4 = Pushbutton [package=THT]
  L1 = Solenoid
  L2 = Solenoid
  L3 = Solenoid
  L4 = Solenoid
  S5 = Pushbutton [package=THT]
  S6 = Pushbutton [package=THT]
  S7 = Pushbutton [package=THT]
  S8 = Pushbutton [package=THT]
  L5 = Solenoid
  R2 = Resistor [tolerance=±5% resistance=10k package=THT]
  R3 = Resistor [tolerance=±5% resistance=10k package=THT]
  R4 = Resistor [tolerance=±5% resistance=10k package=THT]
  R5 = Resistor [tolerance=±5% resistance=10k package=THT]
  Q1 = PNP-Transistor [package="TO92 [THT]"]
  Q2 = PNP-Transistor [package="TO92 [THT]"]
  Q3 = PNP-Transistor [package="TO92 [THT]"]
  Q4 = PNP-Transistor [package="TO92 [THT]"]
  Q5 = PNP-Transistor [package="TO92 [THT]"]
  R6 = Resistor [tolerance=±5% resistance=10k package=THT]
  L6 = Solenoid
  L7 = Solenoid
  L8 = Solenoid
  L9 = Solenoid
  U1 = mystery part, 2 pins
  U2 = mystery part, 2 pins
  U3 = mystery part, 2 pins
  U4 = mystery part, 2 pins

nets:
  N1: V1.V+, S1.leg0, S2.leg0, S3.leg0, S4.leg0, L5.pin1, L6.pin1, L7.pin1
  GND: V1.V-, L1.pin1, L2.pin1, L3.pin1, L4.pin1, R2.Pin_1, R3.Pin_1, R4.Pin_1, R5.Pin_1, Q2.E, Q5.E
  N2: S1.leg1, L3.pin2
  N3: S2.leg1, L1.pin2
  N4: S3.leg1, L2.pin2
  N5: S4.leg1, L4.pin2
  N6: S5.leg0, U1.pin2
  N7: S5.leg1, R3.Pin_0, Q2.B, U1.pin1
  N8: S6.leg0, U2.pin1
  N9: S6.leg1, R4.Pin_0, Q1.B
  N10: S7.leg0, U3.pin1
  N11: S7.leg1, R5.Pin_0, Q3.B
  N12: S8.leg0, U4.pin1
  N13: S8.leg1, R2.Pin_0, Q4.B
  N14: L5.pin2, Q5.C
  N15: Q1.E, U2.pin2
  N16: Q1.C, L8.pin2
  N17: Q2.C, L9.pin2
  N18: Q3.E, U3.pin2
  N19: Q3.C, L7.pin2
  N20: Q4.E, U4.pin2
  N21: Q4.C, L6.pin2
  N22: Q5.B, R6.Pin_0
  N23: L8.pin1, L9.pin1
